# Fritzing sketch CoffeePort (saved by Fritzing 0.9.3b)
breadboards: 1

parts:
  Arduino1 = Arduino Uno (Rev3)
  U1 = Nokia 6100 Color LCD [package=nokia6100_lcd]
  WeMos_D1_Mini_Relay_Shield_V1 = WeMos D1 Mini Relay Shield V2
  J1 = Piezo Speaker

nets:
  N1: Arduino1.D8, WeMos_D1_Mini_Relay_Shield_V1.D1
  N2: Arduino1.D0/RX, U1.SCK
  N3: Arduino1.D1/TX, U1.DIO
  N4: Arduino1.D7, J1.pin2
  5V: Arduino1.5V, U1.CS, WeMos_D1_Mini_Relay_Shield_V1.5V
  N5: Arduino1.GND, U1.RESET, WeMos_D1_Mini_Relay_Shield_V1.G, J1.pin1

notes:
  5V,TX,RX.GND
  CoffeePort
